# Fritzing sketch PrototypeCircuit (saved by Fritzing 0.9.5d)

parts:
  WeMos_D1_Mini1 = WeMos D1 Mini
  S1 = Pushbutton [package="[THT]"]
  S2 = Pushbutton [package="[THT]"]
  S3 = Pushbutton [package="[THT]"]
  M1 = TP4056 Module [part_number=HW-107]
  WeMos_D1_Mini2 = WeMos D1 Mini
  Digispark1 = Digispark
  U1 = LIPO-110mAh [package=lipo-110]
  Mod1 = KY-008 Laser Transmitter Module [package="Breakout board"]

nets:
  N1: WeMos_D1_Mini1.5V, M1.OUT-#4, Mod1.NC
  N2: WeMos_D1_Mini1.D0, Mod1.S
  N3: WeMos_D1_Mini1.D1, S1.Pin_3, S1.Pin_4
  N4: WeMos_D1_Mini1.D2, S2.Pin_3, S2.Pin_4
  N5: WeMos_D1_Mini1.D3, S3.Pin_3
  N6: WeMos_D1_Mini1.G, S1.Pin_1, S1.Pin_2, S2.Pin_1, S2.Pin_2, S3.Pin_1, S3.Pin_2, M1.OUT-#1, Mod1.-
  N7: M1.BAT-, U1.-
  N8: M1.BAT+, U1.+
  5V: WeMos_D1_Mini2.5V, Digispark1.VCC
  N9: WeMos_D1_Mini2.D3, Digispark1.P0
  N10: WeMos_D1_Mini2.D4, Digispark1.P1
  N11: WeMos_D1_Mini2.G, Digispark1.GND

custom parts:
  WeMos D1 Mini: The D1 mini is a mini wifi board based on ESP-8266EX.
  TP4056 Module: TP4056 Lithium Battery Charge Management Module Links: TP4056 website
  Digispark: The Digispark is an Attiny85 based microcontroller development board similar to the Arduino line, only cheaper, smaller, and a bit less powerful. With a whole host of shields to extend its functionality and the ability to use the familiar Arduino IDE the Digispark is a great way to jump into electronics, or perfect for when an Arduino is too big or too much.
  KY-008 Laser Transmitter Module: KY-008 Laser Transmitter Module, emits a dot shaped red laser beam.
